# Fritzing sketch Tubes Mikom (saved by Fritzing 0.9.3b)

parts:
  A1 = Raspberry Pi 5
  Part1 = Arduino Uno (Rev3)-TopMount
  A2 = MH-FMD buzzer
  Part2 = SRF05 Ultrasonic Rangefinder
  Part3 = SRF05 Ultrasonic Rangefinder
  Part4 = SRF05 Ultrasonic Rangefinder
  MD09B1 = A4988 Stepper Motor Driver Carrier
  U1 = LM2596 step down module  # not connected
  A3 = A4988 driver expansion card
  VCC1 = Battery  # not connected
  M1 = Stepper Motor - 8 wire  # not connected
  CAMERA1 = TTL Serial JPEG Camera

nets:
  5V: A1.5V, A1.Fan-5V, CAMERA1.5V
  GND: A1.GND, CAMERA1.GND
  N1: A1.GPIO15, CAMERA1.TX
  N2: A1.GPIO18, CAMERA1.RX
  N3: A1.GPIO24, CAMERA1.CVBS
  N4: Part1.D8, MD09B1.Enable
  N5: Part1.D9_PWM, MD09B1.DIR
  N6: Part1.D10_PWM/SS, MD09B1.STEP
  N7: Part1.D12/MISO, A2.Pin_2
  N8: Part1.D2, Part3.Trig
  N9: Part1.D3_PWM, Part3.Echo
  N10: Part1.D4, Part2.Trig
  N11: Part1.D5_PWM, Part2.Echo
  N12: Part1.D6_PWM, Part4.VCC, Part4.Trig
  N13: Part1.D7, Part4.Echo
  N14: MD09B1.OUT_2B, MD09B1.OUT_2A, A3.Pin_12, A3.Pin_13
  N15: MD09B1.GROUND, A3.Pin_1, A3.Pin_14

notes:
  Connected to USB Port

custom parts:
  Raspberry Pi 5: The RPi5, a faster version of the awesome Raspberry Pi4B ARM Board with 40 pin gpio.
  Arduino Uno (Rev3)-TopMount: Arduino Uno (Rev3) for Top PCB Mount. The PCB view of the Arduino Uno (Rev3) in Arduino Bin flipped upside down with the text flipped back so as to be readable. Other views haven't changed Protruding component position is outlined to provide indication of part contact. Number in component outline is mm of protrusion of the component from the UNO PCB. Subtract the number from the USB (11mm),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
  MH-FMD buzzer: MH-FMD buzzer.
  LM2596 step down module: LM2596 DC-DC step down power supply module 3 A.
  A4988 driver expansion card: A4988 driver expansion card.
  Battery: Your standard 2x 18650 battery pack (14.7 Volts)
  Stepper Motor - 8 wire: Simple, but very powerful bi polar stepper motor. 8 wire
  TTL Serial JPEG Camera: TTL Serial JPEG Camera with NTSC Out
